# Fritzing sketch Laser Viscometer (saved by Fritzing 0.9.3b)
breadboards: 1

parts:
  Part1 = Arduino Nano (Rev3.0)
  Laser_Switch = Pushbutton [package="[THT]"]
  Laser2 = KY-008 Laser Transmitter Module [package="Breakout board"]
  Laser1 = KY-008 Laser Transmitter Module [package="Breakout board"]
  J1 = Piezo Speaker
  R1 = Resistor [tolerance=±5% resistance=100k package=THT]
  Photodiode_1 = Ambient Light Sensor (TEMT6000 Breakout Board)
  Photodiode_2 = Ambient Light Sensor (TEMT6000 Breakout Board)
  LED1 = LED - 5mm [color="Blue (430nm)" package="5 mm [THT]"]
  LED2 = LED - 5mm [color="Green (570nm)" package="5 mm [THT]"]

nets (from the breadboard view):
  GND: Part1.GND, Laser2.-, Laser1.-, J1.pin1, R1.Pin_1, Photodiode_1.GND, Photodiode_2.GND, LED1.anode, LED2.anode
  N1: Part1.D2, Photodiode_1.S
  N2: Part1.D3, Photodiode_2.S
  N3: Part1.D4, Laser_Switch.Pin_3, Laser_Switch.Pin_4, R1.Pin_0
  N4: Part1.D11/MOSI, J1.pin2
  N5: Part1.D12/MISO, LED2.cathode
  VCC: Part1.5V, Laser_Switch.Pin_1, Laser_Switch.Pin_2, Laser2.S, Laser1.S, Photodiode_1.VCC, Photodiode_2.VCC
  N6: Part1.D13/SCK, LED1.cathode

custom parts:
  KY-008 Laser Transmitter Module: Laser Transmitter module KY-008 for Arduino, emits a dot shaped red laser beam.
